# Fritzing sketch 2-Button-Debounce (saved by Fritzing 0.9.9b)
breadboards: 1

parts:
  Part1 = Arduino Uno (Rev3)
  LED2 = smd LED [color="Green (555nm)" package="1206 [SMD]"]
  R2 = Resistor [tolerance=±1% resistance=220 power=0.25 package=THT]
  S1 = Pushbutton [package="[THT]"]
  R4 = Resistor [tolerance=±1% resistance=10k power=0.25 package=THT]

nets:
  N1: Part1.D11_PWM/MOSI, R2.Pin_0
  N2: Part1.D12/MISO, S1.Pin_1, S1.Pin_2, R4.Pin_1
  N3: Part1.5V, S1.Pin_3, S1.Pin_4
  N4: Part1.GND, LED2.cathode, R4.Pin_0
  N5: LED2.anode, R2.Pin_1
