# Fritzing sketch 4-Serial-In (saved by Fritzing 0.9.9b)
breadboards: 1

parts:
  Part1 = Arduino Uno (Rev3)
  LED2 = smd LED [color="Green (555nm)" package="1206 [SMD]"]
  R2 = Resistor [tolerance=±1% resistance=220 power=0.25 package=THT]

nets:
  N1: Part1.D11_PWM/MOSI, R2.Pin_0
  N2: Part1.GND, LED2.cathode
  N3: LED2.anode, R2.Pin_1
