# Fritzing sketch 5-Analog-LED (saved by Fritzing 0.9.9b)
breadboards: 1

parts:
  Part1 = Arduino Uno (Rev3)
  LED2 = smd LED [color="Green (555nm)" package="1206 [SMD]"]
  R2 = Resistor [tolerance=±1% resistance=220 power=0.25 package=THT]
  R3 = Rotary Potentiometer (Large) [maximum_resistance=100kΩ package=THT]

nets:
  N1: Part1.A0, R3.wiper
  N2: Part1.D11_PWM/MOSI, R2.Pin_0
  N3: Part1.5V, R3.leg1
  N4: Part1.GND, LED2.cathode, R3.leg2
  N5: LED2.anode, R2.Pin_1
