# Fritzing sketch 7-ESP32-LED-Server (saved by Fritzing 0.9.9b)
breadboards: 1

parts:
  R1 = Resistor [tolerance=±1% resistance=220 power=0.25 package=THT]
  LED1 = smd LED [color="Blue (470nm)" package="1206 [SMD]"]
  U1 = ESP32-NodeMCU

nets:
  N1: R1.Pin_0, U1.G25
  N2: R1.Pin_1, LED1.anode
  N3: LED1.cathode, U1.G32, U1.GND#13, U1.SD3, U1.SD0
  N4: U1.G35, U1.G13, U1.CLK
