# Fritzing sketch 8-Everything (saved by Fritzing 0.9.9b)
breadboards: 1

parts:
  R1 = Resistor [tolerance=±1% resistance=220 power=0.25 package=THT]
  LED1 = smd LED [color="Blue (470nm)" package="1206 [SMD]"]
  Part1 = Arduino Uno (Rev3)
  LED2 = smd LED [color="Green (555nm)" package="1206 [SMD]"]
  R2 = Resistor [tolerance=±1% resistance=220 power=0.25 package=THT]
  R3 = Rotary Potentiometer (Large) [maximum_resistance=100kΩ package=THT]
  S1 = Pushbutton [package="[THT]"]
  R4 = Resistor [tolerance=±1% resistance=10k power=0.25 package=THT]
  M1 = Dagu DGServo 9g (Top view) [part_number=RS001B]
  U1 = ESP32-NodeMCU

nets:
  N1: R1.Pin_0, U1.G25
  N2: R1.Pin_1, LED1.anode
  N3: LED1.cathode, U1.G32, U1.GND#13, U1.SD3, U1.SD0
  N4: Part1.A0, R3.wiper
  N5: Part1.D10_PWM/SS, M1.pulse
  N6: Part1.D11_PWM/MOSI, R2.Pin_0
  N7: Part1.D12/MISO, S1.Pin_1, S1.Pin_2, R4.Pin_1
  GND: Part1.GND, LED2.cathode, R3.leg1, R3.leg2, S1.Pin_3, S1.Pin_4, R4.Pin_0, M1.gnd
  5V: Part1.5V, M1.vcc
  N8: LED2.anode, R2.Pin_1
  N9: U1.G35, U1.G13, U1.CLK
